// Digital circuit CPU.dig as structural Verilog
module CPU (
  input  [15:0] A,
  input  [7:0] SD,
  output [15:0] R0,
  output [15:0] R1,
  output [15:0] R2,
  output [15:0] R3,
  output [1:0] Rs,
  output [1:0] rd,
  output [15:0] B,
  output [15:0] A_2
);

  wire button_1_out, button_2_out, execute_1_p3;
  wire [1:0] PC_out;
  wire [31:0] Program_d;

  Counter #(.Bits(2)) PC (.en(1'b1), .C(button_1_out), .clr(1'b0), .out(PC_out));  // open: ovf
  Button button_1 (.out(button_1_out));
  EEPROMDualPort #(.Bits(32)) Program (
    .A(PC_out), .Din({{8{1'b0}}, SD, A}), .str(1'b1), .C(button_2_out), .ld(1'b1), .D(Program_d));
  Button button_2 (.out(button_2_out));
  // Decoder decoder_1: pin names not known; wires that end beside it: Program_d, Rs, A_2, rd
  // Execute execute_1: pin names not known; wires that end beside it: A_2, B, execute_1_p3
  // Registerfile registerfile_1: pin names not known; wires that end beside it: Rs, rd, execute_1_p3, button_1_out, B, R0, R1, R2, R3

  // Notes on the sheet:
  //   A: default 31
  //   SD: default 1
  //   contents of Program (hex, n*v repeats v):
  //   3004d1,1001f,23001f,12001f
  //   =
  //   +
endmodule
